# Fritzing sketch open-tire-pyrometer-circuit (saved by Fritzing 0.9.3b)

parts:
  Part2 = Adafruit Feather nRF52 [part_number="Adafruit #3406"]
  PART1 = SparkFun MAX31855K Thermocouple Breakout [part_number=SEN-13266]
  Part3 = Adafruit Push Button Powerswitch [part_number="Adafruit #1400"]
  R1 = Resistor [tolerance=±1% resistance=10 package=THT]

nets:
  3.3V: Part2.3.3V, PART1.VCC
  GND: Part2.GND, PART1.GND, Part3.GND, R1.Pin_1
  N1: Part2.A0/0.02, PART1.SO
  N2: Part2.A1/0.03, PART1.CS
  N3: Part2.A2/0.04, PART1.SCK
  N4: Part2.P0.16, Part3.OFF
  N5: Part2.EN, Part3.OUT, R1.Pin_0
  N6: Part2.VBAT, Part3.IN

custom parts:
  SparkFun MAX31855K Thermocouple Breakout: The MAX31855K IC takes a standard k-type thermocouple in one end, digitizes the temperature measured and sends that data out the other end via SPI. For more information, please visit www.sparkfun.com
  Adafruit Push Button Powerswitch: The Adafruit Push-button Power Switch is a tidy little design that lets you control a DC power source using an everyday tactile button. The breakout uses a latching analog circuit that is triggered by a push of the button. Press once to turn on, then press again to turn off. The circuit uses a 3A P-FET to connect and disconnect the IN pin to the OUT pin. Works great from 3V to 14VDC and up to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
